# Fritzing sketch jsoknit_proof_of_concept (saved by Fritzing 0.9.2b)
breadboards: 1

parts:
  Part1 = Arduino Uno (Rev3)
  RHT1 = Humidity and Temperature Sensor RHT03
  R1 = Resistor [tolerance=±5% resistance=1k package=THT]
  LED1 = LED - 5mm [color="Red (633nm)" package="5 mm [THT]"]

nets:
  N1: Part1.D9_PWM, R1.Pin_1
  N2: Part1.D2, RHT1.Data-signal
  N3: Part1.D3_PWM, RHT1.Vcc
  N4: Part1.5V, RHT1.GND_2
  N5: Part1.GND, RHT1.GND_1, LED1.cathode
  N6: R1.Pin_0, LED1.anode
